// Logisim project Logisim0基础入门.circ as structural Verilog: 3 circuits, main circuit 从零开始
module \从零开始  (
  input  x,
  input  y,
  output z
);

  and and_1 (z, x, y);
endmodule

module \测试电路  (
);

  \从零开始  \u_从零开始_1  ();  // open: x, z, y
endmodule

module \不同颜色的线缆  (
  input  in_1,
  input  in_2,
  input  in_3,
  input  in_4,
  input  in_5,
  input  [1:0] in_6,
  input  in_7
);

  wire undriven;
  wire [1:0] nand_1_out;
  wire [1:1] undriven_2;

  and and_1 (in_3, in_1, in_2, undriven, in_4);
  assign nand_1_out = ~(in_6 & {undriven_2[1], in_7});  // NAND_Gate nand_1, 2 bits wide
  // Pins of 1 and 2 bits meet at {undriven_2[1], in_7}

  assign in_5 = in_4;
endmodule
